# Fritzing sketch RC car (saved by Fritzing 0.9.4)
breadboards: 1

parts:
  Part1 = Arduino Nano (Rev3.0)
  microSD1 = MicroSD Card Module  # not connected
  Part2 = InvenSense MPU6050
  J1 = Basic Servo
  J2 = Basic Servo
  LED1 = smd LED [color="Red (633nm)" package="0603 [SMD]"]
  R1 = Resistor [tolerance=±5% resistance=220 package="0603 [SMD]"]

nets:
  N1: Part1.D2, Part2.INT
  N2: Part1.D4, LED1.anode
  N3: Part1.D5, J1.pulse
  N4: Part1.D6, J2.pulse
  N5: Part1.A5, Part2.SCL
  N6: Part1.A4, Part2.SDA
  VCC: Part2.VCC, J1.vcc, J2.vcc
  GND: Part2.GND, J1.gnd, J2.gnd, R1.Pin_0
  N7: LED1.cathode, R1.Pin_1
