# Fritzing sketch Lego of death (saved by Fritzing 0.9.4)
breadboards: 1

parts:
  Part1 = Arduino Nano (Rev3.0)
  VCC1 = Battery block 9V
  J1 = Basic Servo
  LED1 = smd LED [color="Red (633nm)" package="0603 [SMD]"]
  LED2 = smd LED [color="Red (633nm)" package="0603 [SMD]"]
  LED3 = smd LED [color="Red (633nm)" package="0603 [SMD]"]
  R1 = Resistor [tolerance=±5% resistance=220 package="1206 [SMD]"]
  R2 = Resistor [tolerance=±5% resistance=220 package="1206 [SMD]"]
  R3 = Resistor [tolerance=±5% resistance=220 package="1206 [SMD]"]

nets:
  N1: Part1.D2, J1.pulse
  N2: Part1.D3, LED3.anode
  N3: Part1.D4, LED1.anode
  N4: Part1.D5, LED2.anode
  N5: VCC1.-, J1.gnd, R1.Pin_0, R2.Pin_0, R3.Pin_0
  N6: VCC1.+, J1.vcc
  N7: LED1.cathode, R2.Pin_1
  N8: LED2.cathode, R1.Pin_1
  N9: LED3.cathode, R3.Pin_1
