# Fritzing sketch Rocks Paper Scissors (saved by Fritzing 0.9.4)
breadboards: 1

parts:
  Part1 = Arduino Uno (Rev3) - ICSP
  U1 = POT [package=pot_mammoth]
  LCD1 = LCD screen
  S1 = SWITCH-MOMENTARY-2 [package=tactile-pth]
  S2 = SWITCH-MOMENTARY-2 [package=tactile-pth]
  S3 = SWITCH-MOMENTARY-2 [package=tactile-pth]
  hc-sr1 = hc-sr04
  R1 = Resistor [tolerance=±5% resistance=220 package="0603 [SMD]"]
  R2 = Resistor [tolerance=±5% resistance=220 package="2512 [SMD]"]
  R3 = Resistor [tolerance=±5% resistance=220 package="2512 [SMD]"]
  R4 = Resistor [tolerance=±5% resistance=220 package="2512 [SMD]"]

nets:
  N1: Part1.D8, R4.Pin_1
  N2: Part1.D9_PWM, hc-sr1.Echo
  N3: Part1.D10_PWM/SS, hc-sr1.Trig
  N4: Part1.D11_PWM/MOSI, LCD1.DB0
  N5: Part1.D12/MISO, LCD1.R/W
  N6: Part1.D2, LCD1.DB7
  N7: Part1.D3_PWM, LCD1.DB6
  N8: Part1.D4, LCD1.DB5
  N9: Part1.D5_PWM, LCD1.DB4
  N10: Part1.D6_PWM, R2.Pin_1
  N11: Part1.D7, R3.Pin_1
  5V: Part1.5V, U1.S, LCD1.VDD, S1.2, S2.2, S3.2, hc-sr1.VCC, R1.Pin_0
  GND: Part1.GND, U1.E, LCD1.VSS, LCD1.E, LCD1.LED-, hc-sr1.GND, R2.Pin_0, R3.Pin_0, R4.Pin_0
  N12: U1.A, LCD1.V0
  N13: LCD1.LED+, R1.Pin_1
